# Fritzing sketch schematic (saved by Fritzing 0.9.10b)
breadboards: 1

parts:
  Controller = Arduino Uno (Rev3) - ICSP
  M1 = Stepper Motor - Bipolar
  M2 = Stepper Motor - Bipolar
  Pololu_A1 = Pololu A4988 [package=SO16]
  Pololu_A2 = Pololu A4988 [package=SO16]
  C1 = Tantalum Capacitor [capacitance="1 μF" voltage=35V package="B 3528 [SMD, tantalum]"]
  C2 = Tantalum Capacitor [capacitance="1 μF" voltage=35V package="B 3528 [SMD, tantalum]"]

nets:
  N1: Controller.ICSP_MOSI, Pololu_A1.STEP
  GND: Controller.GND, Pololu_A1.GND, Pololu_A2.GND, C1.-, C2.-
  N2: Controller.D8, Pololu_A2.DIR
  N3: Controller.D9_PWM, Pololu_A2.STEP
  N4: Controller.D10_PWM/SS, Pololu_A1.DIR
  N5: M1.A, Pololu_A2.2B
  N6: M1.C, Pololu_A2.2A
  N7: M1.B, Pololu_A2.1A
  N8: M1.D, Pololu_A2.1B
  N9: M2.A, Pololu_A1.2B
  N10: M2.C, Pololu_A1.2A
  N11: M2.B, Pololu_A1.1A
  N12: M2.D, Pololu_A1.1B
  5V: Pololu_A1.MS1, Pololu_A1.MS2, Pololu_A1.MS3, Pololu_A1.VDD, Pololu_A2.MS1, Pololu_A2.MS2, Pololu_A2.MS3, Pololu_A2.VDD
  N13: Pololu_A1.RESET, Pololu_A1.SLEEP
  12V: Pololu_A1.VMOT, Pololu_A2.VMOT, C1.+, C2.+
  N14: Pololu_A2.RESET, Pololu_A2.SLEEP
